# Fritzing sketch ArduinoUno_BMP280 (saved by Fritzing 0.9.3b)
breadboards: 1

parts:
  Part1 = Arduino Uno (Rev3)
  Part2 = Adafruit_BMP280

nets:
  N1: Part1.A4/SDA, Part2.SDI/SDA
  N2: Part1.A5/SCL, Part2.SCK/SCL
  5V: Part1.5V, Part2.VIN
  GND: Part1.GND, Part2.GND

custom parts:
  Adafruit_BMP280: Bosch has stepped up their game with their new BMP280 sensor, an environmental sensor with temperature, barometric pressure that is the next generation upgrade to the BMP085/BMP180/BMP183. This sensor is great for all sorts of weather sensing and can even be used in both I2C and SPI! This precision sensor from Bosch is the best low-cost, precision sensing solution for measuring barometric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

// code stored in the sketch: BME280_I2C_Sketch.ino
/***************************************************************************
  This is a library for the BME280 humidity, temperature & pressure sensor
  Designed specifically to work with the BME280 Breakout board
  ----> http://www.adafruit.com/products/2650
  This sketch only supports the I2C bus for connection.
 ***************************************************************************/

#include <Wire.h>
#include "cactus_io_BME280_I2C.h"

// Create the BME280 object
BME280_I2C bme;              // I2C using default 0x77 
// or BME280_I2C bme(0x76);  // I2C using address 0x76

void setup() {
  Serial.begin(9600);
  Serial.println("Bosch BME280 Barometric Pressure - Humidity - Temp Sensor | cactus.io"); 

  if (!bme.begin()) {
    Serial.println("Could not find a valid BME280 sensor, check wiring!");
    while (1);
  }

  bme.setTempCal(-1);
  
  Serial.println("Pressure\tHumdity\t\tTemp\t\tTemp");
  
}

void loop() {

    bme.readSensor(); 
  
    Serial.print(bme.getPressure_MB()); Serial.print("\t\t");    // Pressure in millibars
    Serial.print(bme.getHumidity()); Serial.print("\t\t");
    Serial.print(bme.getTemperature_C()); Serial.print(" *C\t");
    Serial.print(bme.getTemperature_F()); Serial.println(" *F\t");

    // add a 2 second delay to slow down the output
    delay(2000);
}
