# Fritzing sketch Photon_BME280 (saved by Fritzing 0.9.3b)
breadboards: 2

parts:
  Part1 = Photon
  Part2 = Adafruit BME280

nets:
  GND: Part1.GND, Part2.GND
  N1: Part1.D0, Part2.SDI/SDA
  N2: Part1.D1, Part2.SCK/SCL
  3V3: Part1.3V3, Part2.VIN

custom parts:
  Adafruit BME280: Bosch has stepped up their game with their new BME280 sensor, an environmental sensor with temperature, barometric pressure and humidity! This sensor is great for all sorts of weather/environmental sensing and can even be used in both I2C and SPI! This precision sensor from Bosch is the best low-cost sensing solution for measuring humidity with ±3% accuracy, barometric pressure with ±1 hPa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

// code stored in the sketch: bme280_Photon.ino
// Distributed with a free-will license.
// Use it any way you want, profit or free, provided it fits in the licenses of its associated works.
// BME280
// This code is designed to work with the BME280_I2CS I2C Mini Module available from ControlEverything.com.
// https://www.controleverything.com/content/Humidity?sku=BME280_I2CS#tabs-0-product_tabset-2

#include <application.h>
#include <spark_wiring_i2c.h>

// BME280 I2C address is 0x76(108)
#define Addr 0x77

double cTemp = 0, fTemp = 0, pressure = 0, humidity = 0;
void setup() 
{
    // Set variable
    Particle.variable("i2cdevice", "BME280");
    Particle.variable("cTemp", cTemp);
    Particle.variable("fTemp", fTemp);
    Particle.variable("pressure", pressure);
    Particle.variable("humidity", humidity);
    
    // Initialise I2C communication as MASTER
    Wire.begin();
    // Initialise Serial communication, set baud rate = 9600
    Serial.begin(9600);
    delay(300);
}

void loop()
{
    unsigned int b1[24];
    unsigned int data[8];
    int dig_H1 = 0;
    for(int i = 0; i < 24; i++)
    {
        // Start I2C Transmission
        Wire.beginTransmission(Addr);
        // Select data register
        Wire.write((136+i));
        // Stop I2C Transmission
        Wire.endTransmission();
        
        // Request 1 byte of data
        Wire.requestFrom(Addr, 1);
        
        // Read 24 bytes of data
        if(Wire.available() == 1)
        {
        b1[i] = Wire.read();
        }
    }
    
    // Convert the data
    // temp coefficents
    int dig_T1 = (b1[0] & 0xff) + ((b1[1] & 0xff) * 256);
    int dig_T2 = b1[2] + (b1[3] * 256);
    int dig_T3 = b1[4] + (b1[5] * 256);
    
    // pressure coefficents
    int dig_P1 = (b1[6] & 0xff) + ((b1[7] & 0xff ) * 256);
    int dig_P2 = b1[8] + (b1[9] * 256);
    int dig_P3 = b1[10] + (b1[11] * 256);
    int dig_P4 = b1[12] + (b1[13] * 256);
    int dig_P5 = b1[14] + (b1[15] * 256);
    int dig_P6 = b1[16] + (b1[17] * 256);
    int dig_P7 = b1[18] + (b1[19] * 256);
    int dig_P8 = b1[20] + (b1[21] * 256);
    int dig_P9 = b1[22] + (b1[23] * 256);
    
    for(int i = 0; i < 7; i++)
    {
        // Start I2C Transmission
        Wire.beginTransmission(Addr);
        // Select data register
        Wire.write((225+i));
        // Stop I2C Transmission
        Wire.endTransmission();
        
        // Request 1 byte of data
        Wire.requestFrom(Addr, 1);
        
        // Read 7 bytes of data
        if(Wire.available() == 1)
        {
            b1[i] = Wire.read();
        }
    }
    
    // Convert the data
    // humidity coefficents
    int dig_H2 = b1[0] + (b1[1] * 256);
    int dig_H3 = b1[2] & 0xFF ;
    int dig_H4 = (b1[3] * 16) + (b1[4] & 0xF);
    int dig_H5 = (b1[4] / 16) + (b1[5] * 16);
    int dig_H6 = b1[6];
    
    // Start I2C Transmission
    Wire.beginTransmission(Addr);
    // Select data register
    Wire.write(161);
    // Stop I2C Transmission
    Wire.endTransmission();
    
    // Request 1 byte of data
    Wire.requestFrom(Addr, 1);
    
    // Read 1 byte of data
    if(Wire.available() == 1)
    {
        dig_H1 = Wire.read();
    }
    
    // Start I2C Transmission
    Wire.beginTransmission(Addr);
    // Select control humidity register
    Wire.write(0xF2);
    // Humidity over sampling rate = 1
    Wire.write(0x01);
    // Stop I2C Transmission
    Wire.endTransmission();
    
    // Start I2C Transmission
    Wire.beginTransmission(Addr);
    // Select control measurement register
    Wire.write(0xF4);
    // Normal mode, temp and pressure over sampling rate = 1
    Wire.write(0x27);
    // Stop I2C Transmission
    Wire.endTransmission();
    
    // Start I2C Transmission
    Wire.beginTransmission(Addr);
    // Select config register
    Wire.write(0xF5);
    // Stand_by time = 1000ms
    Wire.write(0xA0);
    // Stop I2C Transmission
    Wire.endTransmission();
    
    for(int i = 0; i < 8; i++)
    {
        // Start I2C Transmission
        Wire.beginTransmission(Addr);
        // Select data register
        Wire.write((247+i));
        // Stop I2C Transmission
        Wire.endTransmission();
        
        // Request 1 byte of data
        Wire.requestFrom(Addr, 1);
        
        // Read 8 bytes of data
        if(Wire.available() == 1)
        {
            data[i] = Wire.read();
        }   
    }
    
    // Convert pressure and temperature data to 19-bits
    long adc_p = (((long)(data[0] & 0xFF) * 65536) + ((long)(data[1] & 0xFF) * 256) + (long)(data[2] & 0xF0)) / 16;
    long adc_t = (((long)(data[3] & 0xFF) * 65536) + ((long)(data[4] & 0xFF) * 256) + (long)(data[5] & 0xF0)) / 16;
    // Convert the humidity data
    long adc_h = ((long)(data[6] & 0xFF) * 256 + (long)(data[7] & 0xFF));
    
    // Temperature offset calculations
    double var1 = (((double)adc_t) / 16384.0 - ((double)dig_T1) / 1024.0) * ((double)dig_T2);
    double var2 = ((((double)adc_t) / 131072.0 - ((double)dig_T1) / 8192.0) *
    (((double)adc_t)/131072.0 - ((double)dig_T1)/8192.0)) * ((double)dig_T3);
    double t_fine = (long)(var1 + var2);
    double cTemp = (var1 + var2) / 5120.0;
    double fTemp = cTemp * 1.8 + 32;
    
    // Pressure offset calculations
    var1 = ((double)t_fine / 2.0) - 64000.0;
    var2 = var1 * var1 * ((double)dig_P6) / 32768.0;
    var2 = var2 + var1 * ((double)dig_P5) * 2.0;
    var2 = (var2 / 4.0) + (((double)dig_P4) * 65536.0);
    var1 = (((double) dig_P3) * var1 * var1 / 524288.0 + ((double) dig_P2) * var1) / 524288.0;
    var1 = (1.0 + var1 / 32768.0) * ((double)dig_P1);
    double p = 1048576.0 - (double)adc_p;
    p = (p - (var2 / 4096.0)) * 6250.0 / var1;
    var1 = ((double) dig_P9) * p * p / 2147483648.0;
    var2 = p * ((double) dig_P8) / 32768.0;
    double pressure = (p + (var1 + var2 + ((double)dig_P7)) / 16.0) / 100 ;
    
    // Humidity offset calculations
    double var_H = (((double)t_fine) - 76800.0);
    var_H = (adc_h - (dig_H4 * 64.0 + dig_H5 / 16384.0 * var_H)) * (dig_H2 / 65536.0 * (1.0 + dig_H6 / 67108864.0 * var_H * (1.0 + dig_H3 / 67108864.0 * var_H))); 
    double humidity = var_H * (1.0 -  dig_H1 * var_H / 524288.0);
    if(humidity > 100.0)
    {
        humidity = 100.0;
    }
    else if(humidity < 0.0) 
    {
        humidity = 0.0;
    }
    
    // Output data to dashboard
    Particle.publish("Temperature in Celsius : ", String(cTemp));
    Particle.publish("Temperature in Fahrenheit : ", String(fTemp));
    Particle.publish("Pressure : ", String(pressure));
    Particle.publish("Relative Humidity : ", String(humidity));
    delay(1000);
}
